# Fritzing sketch  Controlando tiras de leds RGB via serie (saved by Fritzing 0.9.3b)
breadboards: 1

parts:
  Componente1 = Arduino Uno (Rev3)
  RGB_Strip_LED1 = RGB Strip LED
  Q2 = Basic FET N-Channel [package="D2Pak [SMD]"]
  Q3 = Basic FET N-Channel [package="D2Pak [SMD]"]
  Q4 = Basic FET N-Channel [package="D2Pak [SMD]"]
  J2 = Power Jack [package=power_jack_smd]

nets:
  N1: Componente1.D9_PWM, Q4.Gate
  N2: Componente1.D10_PWM/SS, Q3.Gate
  N3: Componente1.D11_PWM/MOSI, Q2.Gate
  N4: Componente1.GND, Q2.source, Q3.source, Q4.source, J2.GNDBREAK
  N5: RGB_Strip_LED1.Common_Connect#4, J2.GND
  N6: RGB_Strip_LED1.Blue_Connect#5, Q4.drain
  N7: RGB_Strip_LED1.Red_Connect#6, Q3.drain
  N8: RGB_Strip_LED1.Green_Connect#7, Q2.drain

notes:
  Entrada de 12V
  LEDs RGB a 12V

custom parts:
  RGB Strip LED: A tri-color Strip LED with red, green and blue. Pin order: red - common cathode - blue - green
