# Fritzing sketch 6.1 Salida digital Inversa (saved by Fritzing 0.9.3b)
breadboards: 1

parts:
  part = Arduino Uno (Rev3)
  LED1 = LED - 5mm [color="Red (633nm)" package="5 mm [THT]"]
  R1 = Resistor [tolerance=±5% resistance=220 package=THT]

nets:
  N1: part.D11_PWM/MOSI, R1.Pin_1
  N2: part.5V, LED1.anode
  N3: LED1.cathode, R1.Pin_0
