# Fritzing sketch 6.11 RGB Catodo comun (saved by Fritzing 0.9.3b)
breadboards: 1

parts:
  R1 = Resistor [tolerance=±5% resistance=220 package=THT]
  LED1 = RGB LED (com. cathode, rgb) [package="5 mm [THT]"]
  Componente1 = Arduino Uno (Rev3)
  R2 = Resistor [tolerance=±5% resistance=220 package=THT]
  R3 = Resistor [tolerance=±5% resistance=220 package=THT]

nets:
  N1: R1.Pin_0, Componente1.D11_PWM/MOSI
  N2: R1.Pin_1, LED1.red_anode
  N3: LED1.common_cathode, Componente1.GND
  N4: LED1.green_anode, R2.Pin_1
  N5: LED1.blue_anode, R3.Pin_1
  N6: Componente1.D9_PWM, R3.Pin_0
  N7: Componente1.D10_PWM/SS, R2.Pin_0
