# Fritzing sketch 6.13 Controlando dispositivos reales (saved by Fritzing 0.9.3b)
breadboards: 1

parts:
  Componente1 = Arduino Uno (Rev3)
  Q2 = Basic FET N-Channel [package="D2Pak [SMD]"]
  RGB_Strip_LED1 = RGB Strip LED
  R1 = Resistor [tolerance=±5% resistance=220 package=THT]
  Q3 = Basic FET N-Channel [package="D2Pak [SMD]"]
  R2 = Resistor [tolerance=±5% resistance=220 package=THT]
  Q4 = Basic FET N-Channel [package="D2Pak [SMD]"]
  R3 = Resistor [tolerance=±5% resistance=220 package=THT]

nets:
  N1: Componente1.D9_PWM, R3.Pin_1
  N2: Componente1.D10_PWM/SS, R2.Pin_1
  N3: Componente1.D11_PWM/MOSI, R1.Pin_1
  N4: Componente1.GND, Q2.source, Q3.source, Q4.source
  N5: Componente1.VIN, RGB_Strip_LED1.Common_Connect#4
  N6: Q2.Gate, R1.Pin_0
  N7: Q2.drain, RGB_Strip_LED1.Green_Connect#7
  N8: RGB_Strip_LED1.Blue_Connect#5, Q4.drain
  N9: RGB_Strip_LED1.Red_Connect#6, Q3.drain
  N10: Q3.Gate, R2.Pin_0
  N11: Q4.Gate, R3.Pin_0

custom parts:
  RGB Strip LED: A tri-color Strip LED with red, green and blue. Pin order: red - common cathode - blue - green
