# Fritzing sketch 6.13 Rele (saved by Fritzing 0.9.3b)

parts:
  KY-1 = Keyes Relay [package=THT]
  Componente1 = Arduino Uno (Rev3)
  LED1 = LEDs [package=led10mm]
  J1 = Power Jack [package=power_jack_pth_lock]

nets:
  N1: KY-1.signal, Componente1.D11_PWM/MOSI
  N2: KY-1.power, Componente1.5V
  N3: KY-1.ground, Componente1.GND
  N4: KY-1.C, J1.GND
  N5: KY-1.NO, LED1.C
  N6: LED1.A, J1.GNDBREAK

custom parts:
  Keyes Relay: The Keyes 5V relay module is suitable for SCM development, home appliance control. It uses a 5V~12V TIL control signal which can control DC / AC signal.
  LEDs: LEDs Standard schematic elements and footprints for 5mm, 3mm, 1206, and 0603 sized LEDs. 5mm - Spark Fun Electronics SKU : COM-00529 (and others)
