# Fritzing sketch 6.6 Scanner Larson o cyllon (saved by Fritzing 0.9.3b)
breadboards: 1

parts:
  Componente1 = Arduino Uno (Rev3)
  R1 = Resistor [tolerance=±5% resistance=220 package=THT]
  LED1 = LED - 5mm [color="Red (633nm)" package="5 mm [THT]"]
  LED2 = LED - 5mm [color="Red (633nm)" package="5 mm [THT]"]
  R2 = Resistor [tolerance=±5% resistance=220 package=THT]
  R3 = Resistor [tolerance=±5% resistance=220 package=THT]
  LED3 = LED - 5mm [color="Red (633nm)" package="5 mm [THT]"]
  LED4 = LED - 5mm [color="Red (633nm)" package="5 mm [THT]"]
  R4 = Resistor [tolerance=±5% resistance=220 package=THT]
  LED5 = LED - 5mm [color="Red (633nm)" package="5 mm [THT]"]
  R5 = Resistor [tolerance=±5% resistance=220 package=THT]

nets:
  N1: Componente1.D8, LED5.anode
  N2: Componente1.D9_PWM, LED4.anode
  N3: Componente1.D10_PWM/SS, LED3.anode
  N4: Componente1.D11_PWM/MOSI, LED2.anode
  N5: Componente1.D12/MISO, LED1.anode
  N6: Componente1.GND, R1.Pin_0, R2.Pin_0, R3.Pin_0, R4.Pin_0, R5.Pin_0
  N7: R1.Pin_1, LED1.cathode
  N8: LED2.cathode, R2.Pin_1
  N9: R3.Pin_1, LED3.cathode
  N10: LED4.cathode, R4.Pin_1
  N11: LED5.cathode, R5.Pin_1
