# Fritzing sketch 7.11 LDR y  potenciometro (saved by Fritzing 0.9.3b)
breadboards: 1

parts:
  Componente1 = Arduino Uno (Rev3)
  R1 = Photocell (LDR) [package=THT]
  R2 = Resistor [tolerance=±5% resistance=220 package=THT]
  R3 = Rotary Potentiometer (Small) [maximum_resistance=100kΩ package=THT]

nets:
  N1: Componente1.A0, R1.pin_0, R2.Pin_0
  N2: Componente1.A1, R3.wiper
  N3: Componente1.5V, R1.pin_1, R3.leg2
  N4: Componente1.GND, R2.Pin_1, R3.leg1
