# Fritzing sketch 7.2 Pulsador mal (saved by Fritzing 0.9.3b)
breadboards: 1

parts:
  S1 = Pushbutton [package="[THT]"]
  Arduino = Arduino Uno (Rev3)

nets:
  N1: S1.Pin_1, S1.Pin_2, Arduino.D2
  N2: S1.Pin_3, S1.Pin_4, Arduino.5V
