# Fritzing sketch 7.2 Pulsador pullDown (saved by Fritzing 0.9.3b)
breadboards: 1

parts:
  S1 = Pushbutton [package="[THT]"]
  part = Arduino Uno (Rev3)
  R1 = Resistor [tolerance=±5% resistance=10k package=THT]

nets:
  N1: S1.Pin_1, S1.Pin_2, part.D2, R1.Pin_0
  N2: S1.Pin_3, S1.Pin_4, part.5V
  N3: part.GND, R1.Pin_1
