# Fritzing sketch 7.2 Pulsador pullUp (saved by Fritzing 0.9.3b)
breadboards: 1

parts:
  part = Arduino Uno (Rev3)
  R1 = Resistor [tolerance=±5% resistance=10k package=THT]
  S1 = Pushbutton [package="[THT]"]

nets:
  N1: part.GND, S1.Pin_1, S1.Pin_2
  N2: part.D2, R1.Pin_1, S1.Pin_3, S1.Pin_4
  N3: part.5V, R1.Pin_0
