# Fritzing sketch 7.2.2 Buzzer Resistencia (saved by Fritzing 0.9.3b)

parts:
  part = Arduino Uno (Rev3)
  J1 = Piezo Speaker
  R1 = Resistor [tolerance=±5% resistance=220 package=THT]

nets:
  N1: part.GND, J1.pin1
  N2: part.D5_PWM, R1.Pin_0
  N3: J1.pin2, R1.Pin_1
