# Fritzing sketch 7.3 potenciometro (saved by Fritzing 0.9.3b)
breadboards: 1

parts:
  Componente1 = Arduino Uno (Rev3)
  R3 = Rotary Potentiometer (Small) [maximum_resistance=100kΩ package=THT]

nets:
  N1: Componente1.A0, R3.wiper
  N2: Componente1.5V, R3.leg2
  N3: Componente1.GND, R3.leg1
