# Fritzing sketch 7.5 Motores DC - L298 (saved by Fritzing 0.9.3b)

parts:
  S1 = H-Bridge with L298N
  Componente1 = Arduino Uno (Rev3)
  M1 = DC Motor
  M2 = DC Motor
  JACK1 = 2.1mm Barrel Jack with Terminal Block

nets:
  N1: S1.12V, JACK1.POS
  GND: S1.GND, Componente1.GND, JACK1.NEG
  5V: S1.5V, Componente1.5V
  N2: S1.ENA, Componente1.D11_PWM/MOSI
  N3: S1.IN1, Componente1.D10_PWM/SS
  N4: S1.IN2, Componente1.D9_PWM
  N5: S1.IN3, Componente1.D8
  N6: S1.IN4, Componente1.D7
  N7: S1.ENB, Componente1.D6_PWM
  N8: S1.M1-01, M2.pin_2
  N9: S1.M1-02, M2.pin_1
  N10: S1.M2-01, M1.pin_2
  N11: S1.M2-02, M1.pin_1

custom parts:
  H-Bridge with L298N: h-bridge
