# Fritzing sketch 7.5 Motores DC - L9110 (saved by Fritzing 0.9.3b)

parts:
  U1 = L9110 H-bridge module [part_number="L9110 H-bridge"]
  Componente1 = Arduino Uno (Rev3)
  M1 = DC Motor
  M2 = DC Motor

nets:
  N1: U1.B-IA, Componente1.D11_PWM/MOSI
  N2: U1.B-IB, Componente1.D10_PWM/SS
  GND: U1.GND, Componente1.GND
  VCC: U1.VCC, Componente1.5V
  N3: U1.A-IA, Componente1.D6_PWM
  N4: U1.A-IB, Componente1.D5_PWM
  N5: U1.MOTOR_A-A, M1.pin_2
  N6: U1.MOTOR_A-B, M1.pin_1
  N7: U1.MOTOR_B-A, M2.pin_2
  N8: U1.MOTOR_B-B, M2.pin_1
