# Fritzing sketch 7.8.2 Interruptor crepuscular (saved by Fritzing 0.9.3b)
breadboards: 1

parts:
  Componente1 = Arduino Uno (Rev3)
  R1 = Photocell (LDR) [package=THT]
  R2 = Resistor [tolerance=±5% resistance=220 package=THT]
  R3 = Rotary Potentiometer (Small) [maximum_resistance=100kΩ package=THT]
  LED1 = LED - 5mm [color="Red (633nm)" package="5 mm [THT]"]
  R5 = Resistor [tolerance=±5% resistance=220 package=THT]

nets:
  N1: Componente1.A0, R1.pin_0, R2.Pin_0
  N2: Componente1.A1, R3.wiper
  N3: Componente1.D7, R5.Pin_0
  N4: Componente1.5V, R1.pin_1, R3.leg2
  N5: Componente1.GND, R2.Pin_1, R3.leg1, LED1.cathode
  N6: LED1.anode, R5.Pin_1
