# Fritzing sketch 8.4 Servo y potenciometro (saved by Fritzing 0.9.3b)
breadboards: 1

parts:
  Componente1 = Arduino Uno (Rev3)
  R3 = Rotary Potentiometer (Small) [maximum_resistance=100kΩ package=THT]
  J1 = Basic Servo

nets:
  N1: Componente1.A0, R3.wiper
  N2: Componente1.D9_PWM, J1.pulse
  5V: Componente1.5V, R3.leg2, J1.vcc
  GND: Componente1.GND, R3.leg1, J1.gnd
